# Fritzing sketch fritzing (saved by Fritzing 0.9.2b)
breadboards: 1

parts:
  Eleman1 = Arduino Mega 2560 (Rev3)
  J1 = Basic Servo
  J2 = Basic Servo
  J3 = Basic Servo
  TCS1 = TCS3200
  TFT1 = Color 320x240 TFT Display, ILI9341 Controller Chip
  R1 = Resistor [tolerance=±5% resistance=1k package=THT]
  R2 = Resistor [tolerance=±5% resistance=1k package=THT]
  R3 = Resistor [tolerance=±5% resistance=1k package=THT]
  R4 = Resistor [tolerance=±5% resistance=1k package=THT]
  R6 = Resistor [tolerance=±5% resistance=1k package=THT]
  R7 = Resistor [tolerance=±5% resistance=1k package=THT]

nets:
  N1: Eleman1.A3, R2.Pin_0
  N2: Eleman1.A4, R7.Pin_0
  N3: Eleman1.A5, R1.Pin_0
  N4: Eleman1.D11_PWM, J1.pulse
  N5: Eleman1.D10_PWM, J2.pulse
  N6: Eleman1.D9_PWM, J3.pulse
  N7: Eleman1.D8_PWM, TCS1.OUT
  N8: Eleman1.3V3, TFT1.LED
  VCC: Eleman1.5V, J1.vcc, J2.vcc, J3.vcc, TCS1.VCC, TFT1.VCC
  GND: Eleman1.GND, J1.gnd, J2.gnd, J3.gnd, TCS1.GND, TFT1.GND
  N9: Eleman1.D4_PWM, TCS1.S0
  N10: Eleman1.D5_PWM, TCS1.S1
  N11: Eleman1.D6_PWM, TCS1.S3
  N12: Eleman1.D7_PWM, TCS1.S2
  N13: Eleman1.D51, R3.Pin_0
  N14: Eleman1.D52, R4.Pin_0
  N15: TFT1.CS, R1.Pin_1
  N16: TFT1.Reset, R6.Pin_1
  N17: TFT1.D/C, R2.Pin_1
  N18: TFT1.SDI_(MOSI), R3.Pin_1
  N19: TFT1.SCK, R4.Pin_1
  N20: R6.Pin_0, R7.Pin_1

notes:
  SERVO BAĞLANTILARI
  9
  10
  11
  TS3200 BAĞLANTILARI
  S1 5
  S0 4
  S3 6
  S2 7
  OUT 8
  9341 TFT BAĞLANTILARI
  CS A5
  RESET A4
  DC A3
  SDI 51
  SCK 52
  LED 3.3V

custom parts:
  TCS3200: COLOR SENSING TCS3200
  Color 320x240 TFT Display, ILI9341 Controller Chip: 2.2" TFT Display with ILI9341 Controller
